# Fritzing sketch prototype (saved by Fritzing 0.9.3b)
breadboards: 2

parts:
  PIR1 = PIR sensor
  J1 = Basic Servo
  LED1 = LED - 3mm [color="Red (633nm)" package="3 mm [THT]"]
  LED2 = LED - 3mm [color="Red (633nm)" package="3 mm [THT]"]
  LED3 = LED - 3mm [color="Red (633nm)" package="3 mm [THT]"]
  F1 = Fan - Ventilador [package=THT]
  Part2 = Jtron 1 Channel Optoisolated Relay Module [package=relay]
  M1 = L293D Motor Driver
  Part3 = Adafruit BMP180
  J2 = Piezo Speaker
  Q1 = TIP120 Hi-Current Darlington Transistor
  Q2 = TIP120 Hi-Current Darlington Transistor
  Q3 = TIP120 Hi-Current Darlington Transistor
  RGB_Strip_LED1 = RGB Strip LED
  Mod1 = MQ-7 breakout
  M2 = DOIT Esp32 DevKit v1 (30 pins long, 11 pins width) [part_number=ESP32S-PIN30]
  R1 = Resistor [tolerance=±5% resistance=1k package=THT]
  R2 = Resistor [tolerance=±5% resistance=1k package=THT]
  R3 = Resistor [tolerance=±5% resistance=1k package=THT]
  LED4 = LEDs [package=led10mm]
  JACK1 = 2.1mm Barrel Jack with Terminal Block

nets:
  VDD: PIR1.VDD, Part3.+3V3, M2.3V3
  N1: PIR1.SIG, M2.D27
  GND: PIR1.GND, J1.gnd, LED1.cathode, LED2.cathode, LED3.cathode, Part2.GND, Part3.GND, J2.pin1, Q1.EMITTER, Q2.EMITTER, Q3.EMITTER, M2.GND, JACK1.NEG
  VCC: J1.vcc, Part2.VCC, Mod1.VCC, M2.VIN
  N2: J1.pulse, M2.D25
  N3: LED1.anode, M2.D4
  N4: LED2.anode, M2.D23
  N5: LED3.anode, M2.D2
  N6: F1.5V, M1.pin_10
  N7: F1.GND, M1.pin_9
  N8: Part2.NO, LED4.A
  N9: Part2.IN1, M2.D15
  N10: M1.pin_5, M2.D33
  N11: M1.pin_6, M2.D32
  N12: Part3.SCL, M2.D22
  N13: Part3.SDA, M2.D21
  N14: J2.pin2, M2.D18
  N15: Q1.BASE, R1.Pin_0
  N16: Q1.COLLECTOR, RGB_Strip_LED1.Blue_Connect
  N17: Q2.BASE, R2.Pin_0
  N18: Q2.COLLECTOR, RGB_Strip_LED1.Green_Connect
  N19: Q3.BASE, R3.Pin_0
  N20: Q3.COLLECTOR, RGB_Strip_LED1.Red_Connect
  N21: RGB_Strip_LED1.Common_Connect, JACK1.POS
  N22: Mod1.AO, M2.D35
  N23: M2.D14, R1.Pin_1
  N24: M2.D12, R2.Pin_1
  N25: M2.D13, R3.Pin_1

notes:
  240V AC Power Supply
  Schematic By: Utsav Sapkota | University ID: 77190014
  9V 1A Power

custom parts:
  Fan - Ventilador: Ventilador de 2 pines, se encuentra comunmente en computadoras de escritorio
  Adafruit BMP180: This precision sensor from Bosch is the best low-cost sensing solution for measuring barometric pressure and temperature. Because pressure changes with altitude you can also use it as an altimeter! The sensor is soldered onto a PCB with a 3.3V regulator, I2C level shifter and pull-up resistors on the I2C pins. The BMP180 is the next-generation of sensors from Bosch, and replaces the BMP085.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
  RGB Strip LED: A tri-color Strip LED with red, green and blue. Based on LED SMD 5050 RGB Pin order: common cathode - green - red - blue
  MQ-7 breakout: MQ-2 gas sensor
  DOIT Esp32 DevKit v1 (30 pins long, 11 pins width): The DOIT Esp32 DevKit v1 is one of the development board created by DOIT to evaluate the ESP-WROOM-32 module. It is based on the ESP32 microcontroller that boasts Wifi, Bluetooth, Ethernet and Low Power support all in a single chip. (vanepp) made breadboard work, adjusted pin numbering and labels and reduced size of schematic and cleaned up pcb. This chip is 30pins long (2 x15) and 11 pins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
  LEDs: LEDs Standard schematic elements and footprints for 5mm, 3mm, 1206, and 0603 sized LEDs. 5mm - Spark Fun Electronics SKU : COM-00529 (and others)
