# Fritzing sketch prototype (saved by Fritzing 0.9.3b)
breadboards: 1

parts:
  PIR1 = PIR sensor  # not connected
  J1 = Basic Servo  # not connected
  LED1 = LED - 3mm [color="Red (633nm)" package="3 mm [THT]"]  # not connected
  LED2 = LED - 3mm [color="Red (633nm)" package="3 mm [THT]"]  # not connected
  LED3 = LED - 3mm [color="Red (633nm)" package="3 mm [THT]"]  # not connected
  F1 = Fan - Ventilador [package=THT]
  Part2 = Jtron 1 Channel Optoisolated Relay Module [package=relay]  # not connected
  M1 = L293D Motor Driver
  Part3 = Adafruit BMP180  # not connected
  J2 = Piezo Speaker  # not connected
  Q1 = TIP120 Hi-Current Darlington Transistor  # not connected
  Q2 = TIP120 Hi-Current Darlington Transistor  # not connected
  Q3 = TIP120 Hi-Current Darlington Transistor  # not connected
  RGB_Strip_LED1 = RGB Strip LED  # not connected
  Mod1 = MQ-7 breakout
  M2 = DOIT Esp32 DevKit v1 (30 pins long, 11 pins width) [part_number=ESP32S-PIN30]

nets:
  N1: F1.5V, M1.pin_10
  N2: F1.GND, M1.pin_9
  N3: Mod1.AO, M2.D35

custom parts:
  Fan - Ventilador: Ventilador de 2 pines, se encuentra comunmente en computadoras de escritorio
  Adafruit BMP180: This precision sensor from Bosch is the best low-cost sensing solution for measuring barometric pressure and temperature. Because pressure changes with altitude you can also use it as an altimeter! The sensor is soldered onto a PCB with a 3.3V regulator, I2C level shifter and pull-up resistors on the I2C pins. The BMP180 is the next-generation of sensors from Bosch, and replaces the BMP085.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
  RGB Strip LED: A tri-color Strip LED with red, green and blue. Based on LED SMD 5050 RGB Pin order: common cathode - green - red - blue
  MQ-7 breakout: MQ-2 gas sensor
  DOIT Esp32 DevKit v1 (30 pins long, 11 pins width): The DOIT Esp32 DevKit v1 is one of the development board created by DOIT to evaluate the ESP-WROOM-32 module. It is based on the ESP32 microcontroller that boasts Wifi, Bluetooth, Ethernet and Low Power support all in a single chip. (vanepp) made breadboard work, adjusted pin numbering and labels and reduced size of schematic and cleaned up pcb. This chip is 30pins long (2 x15) and 11 pins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
